# Fritzing sketch project (saved by Fritzing 0.9.3b)

parts:
  VALVE1 = Plastic Solenoid Valve  # not connected
  VCC1 = Battery block 9V  # not connected
  KY-1 = Keyes Relay [package=THT]
  Raspberry_Pi_2 = Raspberry Pi 4 [part_number=RPI-4-b]
  PSU1 = Adjustable Breadboard Power Supply

nets:
  N1: KY-1.power, Raspberry_Pi_2.3v3
  N2: KY-1.ground, Raspberry_Pi_2.GND
  N3: KY-1.NO, PSU1.Vin2+

custom parts:
  Keyes Relay: The Keyes 5V relay module is suitable for SCM development, home appliance control. It uses a 5V~12V TIL control signal which can control DC / AC signal.
  Raspberry Pi 4: The RPi4, a faster version of the awesome Raspberry Pi 2 B ARM Board with 40 pin gpio. Ready for special Raspberry Pi B+ and RPi2 Hat (Hardware attached (on) top)
